# Fritzing sketch final (saved by Fritzing 0.9.3b)
breadboards: 1

parts:
  Composant1 = Arduino Uno (Rev3)
  R2 = Resistor [tolerance=±5% resistance=100 package=THT]
  L2 = Inductors [package=b82462g]
  R1 = Resistor [tolerance=±5% resistance=1M package="2512 [SMD]"]
  LED1 = LED - 5mm [color="Green (560nm)" package="5 mm [THT]"]
  LED2 = smd LED [color="Red (633nm)" package="1206 [SMD]"]
  R5 = Resistor [tolerance=±5% resistance=220 package="2512 [SMD]"]
  R6 = Resistor [tolerance=±5% resistance=220 package="2512 [SMD]"]
  LED3 = smd LED [color="Yellow (595nm)" package="1206 [SMD]"]
  R3 = Resistor [tolerance=±5% resistance=3.30k package="0603 [SMD]"]

nets:
  N1: Composant1.A0, L2.2
  N2: Composant1.D9_PWM, R2.Pin_1
  N3: Composant1.GND, LED1.cathode, LED2.anode, LED3.cathode, R3.Pin_0
  N4: Composant1.D4, R1.Pin_1
  N5: Composant1.D5_PWM, R5.Pin_0
  N6: Composant1.D6_PWM, R6.Pin_1
  N7: R2.Pin_0, L2.1
  N8: R1.Pin_0, LED1.anode
  N9: LED2.cathode, R5.Pin_1
  N10: R6.Pin_0, LED3.anode
  GND: R3.Pin_1
