# Fritzing sketch shéma (platine + representation) 1 (saved by Fritzing 0.9.3b)
breadboards: 1

parts:
  Composant1 = Arduino Uno (Rev3)
  R2 = Resistor [tolerance=±5% resistance=100 package=THT]
  L2 = Inductors [package=b82462g]
  R1 = Resistor [tolerance=±5% resistance=1M package="2512 [SMD]"]

nets:
  électrode: Composant1.A0, L2.1, R1.Pin_0
  N1: Composant1.D9_PWM, R2.Pin_0
  GND: Composant1.GND, R1.Pin_1
  N2: R2.Pin_1, L2.2
