# Fritzing sketch shéma 2b(représentation) (saved by Fritzing 0.9.3b)
breadboards: 1

parts:
  Composant1 = Arduino Uno (Rev3)
  R2 = Resistor [tolerance=±5% resistance=100 package=THT]
  L2 = Inductors [package=b82462g]
  R1 = Resistor [tolerance=±5% resistance=1M package="2512 [SMD]"]
  D1 = Diode [package=diode-1n4148]
  C1 = Ceramic Capacitor [capacitance=100µF package="0603 [SMD, multilayer]"]
  C3 = Ceramic Capacitor [capacitance=10nF package="1206 [SMD, multilayer]"]
  R3 = Resistor [tolerance=±5% resistance=3.30k package="0603 [SMD]"]

nets (from the schematic view):
  N1: Composant1.A0, R1.Pin_0, D1.C, C1.1
  N2: Composant1.D9_PWM, R2.Pin_0
  N3: Composant1.GND, R1.Pin_1, C1.0
  N4: R2.Pin_1, L2.2, R3.Pin_0
  N5: L2.1, D1.A, C3.1
  électrode: C3.0
  GND: R3.Pin_1
