# Fritzing sketch shéma2a (platine) (saved by Fritzing 0.9.3b)
breadboards: 1

parts:
  Composant1 = Arduino Uno (Rev3)
  R2 = Resistor [tolerance=±5% resistance=100 package=THT]
  L2 = Inductors [package=b82462g]
  R1 = Resistor [tolerance=±5% resistance=1M package="2512 [SMD]"]
  D1 = Diode [package=diode-1n4148]
  C1 = Ceramic Capacitor [capacitance=100µF package="0603 [SMD, multilayer]"]
  C3 = Ceramic Capacitor [capacitance=10nF package="1206 [SMD, multilayer]"]
  R3 = Resistor [tolerance=±5% resistance=3.30k package="0603 [SMD]"]

nets:
  N1: Composant1.A0, Composant1.GND, R2.Pin_1, R1.Pin_0, R1.Pin_1, C3.1, R3.Pin_0
  N2: Composant1.D9_PWM, R2.Pin_0
  N3: L2.1, C1.0
  GND: L2.2, R3.Pin_1
  N4: D1.C, C1.1
  électrode: C3.0
